# Fritzing sketch rpi leds (saved by Fritzing 0.9.3b)
breadboards: 1

parts:
  LED1 = LED - 5mm [color="Red (633nm)" package="5 mm [THT]"]
  R1 = Resistor [tolerance=±5% resistance=220 package=THT]
  LED2 = LED - 5mm [color="Orange (612nm)" package="5 mm [THT]"]
  LED3 = LED - 5mm [color="Green (555nm)" package="5 mm [THT]"]
  R2 = Resistor [tolerance=±5% resistance=220 package=THT]
  R3 = Resistor [tolerance=±5% resistance=220 package=THT]
  S1 = Pushbutton [package="[THT]"]
  Raspberry_Pi_Zero1 = Raspberry Pi Zero
  S2 = Toggle Switch [package=THT]

nets:
  N1: LED1.cathode, R1.Pin_1
  N2: LED1.anode, Raspberry_Pi_Zero1.GPIO17
  N3: R1.Pin_0, R2.Pin_0, R3.Pin_0, S1.Pin_1, S1.Pin_2, S1.Pin_3, S1.Pin_4, Raspberry_Pi_Zero1.GND, S2.L1
  N4: LED2.cathode, R3.Pin_1
  N5: LED2.anode, Raspberry_Pi_Zero1.GPIO27
  N6: LED3.cathode, R2.Pin_1
  N7: LED3.anode, Raspberry_Pi_Zero1.GPIO22
